// Logisim project ex1.circ as structural Verilog: 6 circuits, main circuit NOR1
module NAND1 (
  input  A,
  input  B,
  output RESULT
);

  wire and_1_out;

  and and_1 (and_1_out, A, B);
  not not_1 (RESULT, and_1_out);

  // Notes on the sheet:
  //   PUT CIRCUITRY HERE
endmodule

module NOR1 (
  input  A,
  input  B,
  output RESULT
);

  wire or_1_out;

  or or_1 (or_1_out, A, B);
  not not_1 (RESULT, or_1_out);

  // Notes on the sheet:
  //   PUT CIRCUITRY HERE
endmodule

module XOR1 (
  input  A,
  input  B,
  output RESULT
);

  wire and_1_out, and_2_out, not_1_out, not_2_out;

  not not_1 (not_1_out, A);
  not not_2 (not_2_out, B);
  and and_1 (and_1_out, not_1_out, B);
  and and_2 (and_2_out, A, not_2_out);
  or or_1 (RESULT, and_1_out, and_2_out);

  // Notes on the sheet:
  //   PUT CIRCUITRY HERE
endmodule

module MUX2 (
  input  A,
  input  B,
  input  Sel,
  output RESULT
);

  wire and_1_out, and_2_out, not_1_out;

  and and_1 (and_1_out, B, Sel);
  not not_1 (not_1_out, Sel);
  and and_2 (and_2_out, A, not_1_out);
  or or_1 (RESULT, and_2_out, and_1_out);

  // Notes on the sheet:
  //   PUT CIRCUITRY HERE
endmodule

module MUX4 (
  input  A,
  input  B,
  input  C,
  input  D,
  input  Sel1,
  input  Sel2,
  output RESULT
);

  wire and_1_out, and_2_out, and_3_out, and_4_out, not_1_out, not_2_out;

  and and_1 (and_1_out, D, Sel1, Sel2);
  not not_1 (not_1_out, Sel1);
  not not_2 (not_2_out, Sel2);
  and and_2 (and_2_out, C, Sel2, not_1_out);
  and and_3 (and_3_out, B, Sel1, not_2_out);
  and and_4 (and_4_out, A, not_1_out, not_2_out);
  or or_1 (RESULT, and_4_out, and_3_out, and_2_out, and_1_out);

  // Notes on the sheet:
  //   PUT CIRCUITRY HERE
endmodule

module Half_Adder (
  input  A,
  input  B,
  output SUM,
  output CARRY
);

  XOR1 xor1_1 (.A(A), .B(B), .RESULT(SUM));
  and and_1 (CARRY, A, B);
endmodule
