// Logisim project ex1.circ as structural Verilog: 4 circuits, main circuit main
module main (
  output [7:0] non_pipe_out,
  output [7:0] pipe_out
);

  wire CLK_out;
  wire [7:0] Address_Counter_q, rom_1_data;

  Counter Address_Counter (.clk(CLK_out), .Q(Address_Counter_q));  // open: clr, load, up, count, D, carry
  Clock CLK (.out(CLK_out));
  ROM rom_1 (.addr(Address_Counter_q), .data(rom_1_data));
  // Probe on non_pipe_out
  non_pipelined non_pipelined_1 (.in1(rom_1_data[3:0]), .in2(rom_1_data[7:4]), .CLK(CLK_out), .out1(non_pipe_out));
  // Probe on pipe_out
  pipelined pipelined_1 (.in1(rom_1_data[3:0]), .in2(rom_1_data[7:4]), .CLK(CLK_out), .out1(pipe_out));

  // Notes on the sheet:
  //   contents of rom_1 (hex, n*v repeats v):
  //   13 a2 fc 8f 1c 2 b0
endmodule

module non_pipelined (
  input  [3:0] in1,
  input  [3:0] in2,
  input  CLK,
  output [7:0] out1
);

  wire [7:0] move_and_add_1_moved_multiplicand, move_and_add_1_result, move_and_add_2_moved_multiplicand,
       move_and_add_2_result, move_and_add_3_moved_multiplicand, move_and_add_3_result, move_and_add_4_result;

  // Probe on move_and_add_1_result
  move_and_add move_and_add_1 (
    .multiplicand({4'b0000, in1}), .result(move_and_add_1_result), .current({8{1'b0}}), .multiplier(in2[0]),
    .moved_multiplicand(move_and_add_1_moved_multiplicand));
  move_and_add move_and_add_2 (
    .multiplicand(move_and_add_1_moved_multiplicand), .result(move_and_add_2_result),
    .current(move_and_add_1_result), .multiplier(in2[1]),
    .moved_multiplicand(move_and_add_2_moved_multiplicand));
  move_and_add move_and_add_3 (
    .multiplicand(move_and_add_2_moved_multiplicand), .result(move_and_add_3_result),
    .current(move_and_add_2_result), .multiplier(in2[2]),
    .moved_multiplicand(move_and_add_3_moved_multiplicand));
  move_and_add move_and_add_4 (
    .multiplicand(move_and_add_3_moved_multiplicand), .result(move_and_add_4_result),
    .current(move_and_add_3_result), .multiplier(in2[3]));  // open: moved_multiplicand
  Register register_1 (.D(move_and_add_4_result), .clk(CLK), .Q(out1));  // open: en, clr

  // Notes on the sheet:
  //   The most time-costing would be the adder and mux, there are four in total
  //   which sums up to (20+45)*4 + 10 + 10 = 280ns
endmodule

module pipelined (
  input  [3:0] in1,
  input  [3:0] in2,
  input  CLK,
  output [7:0] out1
);

  wire [7:0] adder_1_out, adder_2_out, adder_3_out, multiplexer_1_out, multiplexer_2_out, multiplexer_3_out,
       multiplexer_4_out, shifter_1_out, shifter_2_out, shifter_3_out;
  wire [31:0] register_1_q;

  Multiplexer #(.width(8), .enable("false")) multiplexer_1 (
    .in0({8{1'b0}}), .in1({4'b0000, in1}), .out(multiplexer_1_out), .sel(in2[0]));
  Shifter shifter_1 (.in({4'b0000, in1}), .\dist (3'b001), .out(shifter_1_out));
  Multiplexer #(.width(8), .enable("false")) multiplexer_2 (
    .in0({8{1'b0}}), .in1(shifter_1_out), .out(multiplexer_2_out), .sel(in2[1]));
  Shifter shifter_2 (.in({4'b0000, in1}), .\dist (3'b010), .out(shifter_2_out));
  Multiplexer #(.width(8), .enable("false")) multiplexer_3 (
    .in0({8{1'b0}}), .in1(shifter_2_out), .out(multiplexer_3_out), .sel(in2[2]));
  Shifter shifter_3 (.in({4'b0000, in1}), .\dist (3'b011), .out(shifter_3_out));
  Multiplexer #(.width(8), .enable("false")) multiplexer_4 (
    .in0({8{1'b0}}), .in1(shifter_3_out), .out(multiplexer_4_out), .sel(in2[3]));
  Register #(.width(32)) register_1 (
    .D({multiplexer_4_out, multiplexer_3_out, multiplexer_2_out, multiplexer_1_out}), .clk(CLK),
    .Q(register_1_q));  // open: en, clr
  Adder adder_1 (.a(register_1_q[7:0]), .b(register_1_q[15:8]), .out(adder_1_out));  // open: cin, cout
  Adder adder_2 (.a(register_1_q[23:16]), .b(register_1_q[31:24]), .out(adder_2_out));  // open: cin, cout
  Register register_2 (.D(adder_3_out), .clk(CLK), .Q(out1));  // open: en, clr
  Adder adder_3 (.a(adder_1_out), .b(adder_2_out), .out(adder_3_out));  // open: cin, cout

  // Notes on the sheet:
  //   The longest path would be the two adder, which sums up tp 45+45=90ns
endmodule

module move_and_add (
  input  [7:0] current,
  input  [7:0] multiplicand,
  input  multiplier,
  output [7:0] result,
  output [7:0] moved_multiplicand
);

  wire [7:0] adder_1_out;

  Adder adder_1 (.a(current), .b(multiplicand), .out(adder_1_out));  // open: cin, cout
  Shifter shifter_1 (.in(multiplicand), .\dist (3'b001), .out(moved_multiplicand));
  Multiplexer #(.width(8), .enable("false")) multiplexer_1 (
    .in0(current), .in1(adder_1_out), .out(result), .sel(multiplier));
endmodule
